# Fritzing sketch forest_fire_detection_layout (saved by Fritzing 0.9.3b)

parts:
  Part2 = Adafruit AMG8833 [part_number="Adafruit #3538"]
  Raspberry_Pi_1 = Raspberry Pi 3 [part_number=RPI-3-V1.2]

nets:
  VCC: Part2.VCC, Raspberry_Pi_1.5V
  3.3V: Part2.3.3V, Raspberry_Pi_1.3v3
  GND: Part2.GND, Raspberry_Pi_1.GND
  N1: Part2.SCL, Raspberry_Pi_1.GPIO3
  N2: Part2.SDA, Raspberry_Pi_1.GPIO2

custom parts:
  Adafruit AMG8833: Add heat-vision to your project and with an Adafruit AMG8833 Grid-EYE Breakout! This sensor from Panasonic is an 8x8 array of IR thermal sensors. When connected to your microcontroller (or raspberry Pi) it will return an array of 64 individual infrared temperature readings over I2C. It's like those fancy thermal cameras, but compact and simple enough for easy integration. This part will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
